// Logisim project ComputerTest.circ as structural Verilog: 12 circuits, main circuit main
module main (
  output [31:0] out_1,
  output [23:0] out_2,
  output [2:0] out_3,
  output [25:0] out_4,
  output [31:0] out_5
);

  wire and_1_out, cpu_1_clock, cpu_1_load, cpu_1_store, not_1_out;
  wire [31:0] ram_1_dout, ram_setter_1_byteload, rom_1_data, transistor_1_out;

  ROM #(.addrWidth(24), .dataWidth(32)) rom_1 (.addr(out_2), .data(rom_1_data));
  cpu cpu_1 (
    .instructions(rom_1_data), .ram_data(ram_setter_1_byteload), .func3(out_3), .address(out_4),
    .data(out_5), .pc(out_2), .load(cpu_1_load), .store(cpu_1_store), .clock(cpu_1_clock));
  not not_1 (not_1_out, 1'b1);
  Transistor #(.width(32)) transistor_1 (.in(out_5), .out(transistor_1_out), .gate(not_1_out));
  and and_1 (and_1_out, cpu_1_store, cpu_1_clock);
  RAM #(.addrWidth(24), .dataWidth(32), .trigger("high")) ram_1 (
    .addr(out_4[25:2]), .we(and_1_out), .oe(1'b1), .clk(cpu_1_clock), .dout(ram_1_dout));  // open: din
  RAM_SETTER ram_setter_1 (
    .DATA(transistor_1_out), .MEMORY(ram_1_dout), .FUNC3(out_3), .BYTELOCATION(out_4[1:0]),
    .LOAD(cpu_1_load), .ByteStore(out_1), .ByteLoad(ram_setter_1_byteload));

  // Notes on the sheet:
  //   contents of rom_1 (hex, n*v repeats v):
  //   8093
endmodule

module ALU (
  input  [6:0] func7,
  input  [31:0] rs1,
  input  [31:0] rs2,
  input  [2:0] func3,
  input  [31:0] imm_value,
  input  immediate,
  input  is_active,
  output [31:0] rd
);

  wire and_2_out, comparator_1_gt, comparator_2_gt, not_1_out;
  wire [4:0] multiplexer_1_out;
  wire [31:0] adder_1_out, and_1_out, bit_extender_1_out, bit_extender_2_out, multiplexer_2_out,
       multiplexer_3_out, multiplexer_4_out, or_1_out, shifter_1_out, shifter_2_out, shifter_3_out,
       subtractor_1_out, xor_1_out;
  wire [31:5] multiplexer_1_out_2;

  Multiplexer #(.width(32)) multiplexer_1 (
    .in0(rs2), .in1(imm_value), .out({multiplexer_1_out_2, multiplexer_1_out}), .sel(immediate));
  not not_1 (not_1_out, immediate);
  Adder #(.width(32)) adder_1 (
    .a(rs1), .b({multiplexer_1_out_2, multiplexer_1_out}), .out(adder_1_out));  // open: cin, cout
  Subtractor #(.width(32)) subtractor_1 (
    .a(rs1), .b({multiplexer_1_out_2, multiplexer_1_out}), .out(subtractor_1_out));  // open: bin, bout
  Shifter #(.width(32)) shifter_1 (
    .in({multiplexer_1_out_2, multiplexer_1_out}), .\dist (multiplexer_1_out), .out(shifter_1_out));
  Comparator #(.width(32)) comparator_1 (
    .a(rs1), .b({multiplexer_1_out_2, multiplexer_1_out}), .gt(comparator_1_gt));  // open: eq, lt
  Comparator #(.mode("unsigned"), .width(32)) comparator_2 (
    .a({multiplexer_1_out_2, multiplexer_1_out}), .b({multiplexer_1_out_2, multiplexer_1_out}),
    .gt(comparator_2_gt));  // open: eq, lt
  assign xor_1_out = rs1 ^ {multiplexer_1_out_2, multiplexer_1_out};  // XOR_Gate xor_1, 32 bits wide
  Shifter #(.shift("lr"), .width(32)) shifter_2 (.in(rs1), .\dist (multiplexer_1_out), .out(shifter_2_out));
  Shifter #(.shift("ar"), .width(32)) shifter_3 (.in(rs1), .\dist (multiplexer_1_out), .out(shifter_3_out));
  assign bit_extender_1_out = {{31{comparator_1_gt}}, comparator_1_gt};  // Bit_Extender bit_extender_1
  assign bit_extender_2_out = {{31{comparator_2_gt}}, comparator_2_gt};  // Bit_Extender bit_extender_2
  assign or_1_out = rs1 | {multiplexer_1_out_2, multiplexer_1_out};  // OR_Gate or_1, 32 bits wide
  assign and_1_out = rs1 & {multiplexer_1_out_2, multiplexer_1_out};  // AND_Gate and_1, 32 bits wide
  Multiplexer #(.width(32)) multiplexer_2 (
    .in0(adder_1_out), .in1(subtractor_1_out), .out(multiplexer_2_out), .sel(and_2_out));
  Multiplexer #(.width(32)) multiplexer_3 (
    .in0(shifter_2_out), .in1(shifter_3_out), .out(multiplexer_3_out), .sel(and_2_out));
  and and_2 (and_2_out, func7[5], not_1_out);
  Multiplexer #(.select(3), .width(32)) multiplexer_4 (
    .in0(multiplexer_2_out), .in1(shifter_1_out), .in2(bit_extender_1_out), .in3(bit_extender_2_out),
    .in4(xor_1_out), .in5(multiplexer_3_out), .in6(or_1_out), .in7(and_1_out), .out(multiplexer_4_out),
    .sel(func3));
  assign rd = is_active ? multiplexer_4_out : 32'bz;  // Controlled_Buffer controlled_buffer_1
endmodule

module RAM_SETTER (
  input  [31:0] DATA,
  input  [31:0] MEMORY,
  input  [2:0] FUNC3,
  input  [1:0] BYTELOCATION,
  input  LOAD,
  output [31:0] ByteStore,
  output [31:0] ByteLoad
);

  wire [7:0] multiplexer_3_out;
  wire [15:0] multiplexer_4_out;
  wire [31:0] bit_extender_1_out, bit_extender_2_out, bit_extender_3_out, buffer_1_out, multiplexer_1_out,
       multiplexer_2_out, multiplexer_5_out, multiplexer_6_out;

  assign buffer_1_out = DATA;  // Buffer buffer_1, 32 bits wide
  assign bit_extender_1_out = {{31{LOAD}}, LOAD};  // Bit_Extender bit_extender_1
  Multiplexer #(.width(32)) multiplexer_1 (
    .in0({MEMORY[31:16], buffer_1_out[15:0]}), .in1({buffer_1_out[15:0], MEMORY[15:0]}),
    .out(multiplexer_1_out), .sel(BYTELOCATION[1]));
  Multiplexer #(.select(2), .width(32)) multiplexer_2 (
    .in0({MEMORY[31:8], buffer_1_out[7:0]}), .in1({MEMORY[31:16], buffer_1_out[7:0], MEMORY[7:0]}),
    .in2({MEMORY[31:24], buffer_1_out[7:0], MEMORY[15:0]}), .in3({buffer_1_out[7:0], MEMORY[23:0]}),
    .out(multiplexer_2_out), .sel(BYTELOCATION));
  Multiplexer #(.select(2), .width(8)) multiplexer_3 (
    .in0(MEMORY[7:0]), .in1(MEMORY[15:8]), .in2(MEMORY[23:16]), .in3(MEMORY[31:24]), .out(multiplexer_3_out),
    .sel(BYTELOCATION));
  Multiplexer #(.width(16)) multiplexer_4 (
    .in0(MEMORY[15:0]), .in1(MEMORY[31:16]), .out(multiplexer_4_out), .sel(BYTELOCATION[1]));
  assign bit_extender_2_out = {{24{multiplexer_3_out[7]}}, multiplexer_3_out};  // Bit_Extender bit_extender_2
  assign bit_extender_3_out = {{16{multiplexer_4_out[15]}}, multiplexer_4_out};  // Bit_Extender bit_extender_3
  Multiplexer #(.select(3), .width(32)) multiplexer_5 (
    .in0(multiplexer_2_out), .in1(multiplexer_1_out), .in2(buffer_1_out), .out(multiplexer_5_out), .sel(FUNC3));  // open: in3, in4, in5, in6, in7
  assign ByteStore = {32{1'b0}} | multiplexer_5_out;  // OR_Gate or_1, 32 bits wide
  Multiplexer #(.select(3), .width(32)) multiplexer_6 (
    .in0(bit_extender_2_out), .in1(bit_extender_3_out), .in2(MEMORY), .out(multiplexer_6_out), .sel(FUNC3));  // open: in3, in4, in5, in6, in7
  assign ByteLoad = multiplexer_6_out & bit_extender_1_out;  // AND_Gate and_1, 32 bits wide
endmodule

module bigtransistor (
  input  Gate,
  input  [31:0] Source,
  output [31:0] Drain
);

  wire not_1_out;
  wire [31:0] and_1_out, bit_extender_1_out;

  assign bit_extender_1_out = {{31{Gate}}, Gate};  // Bit_Extender bit_extender_1
  not not_1 (not_1_out, Gate);
  assign and_1_out = bit_extender_1_out & Source;  // AND_Gate and_1, 32 bits wide
  Multiplexer #(.width(32)) multiplexer_1 (.in0(and_1_out), .out(Drain), .sel(not_1_out));  // open: in1
endmodule

module cpu (
  input  [31:0] instructions,
  input  [31:0] ram_data,
  output [2:0] func3,
  output [25:0] address,
  output [31:0] data,
  output [23:0] pc,
  output load,
  output store,
  output clock
);

  wire bus_decoder_1_alu, bus_decoder_1_clockload, bus_decoder_1_is_imm, bus_decoder_1_jump,
       bus_decoder_1_store, condition_evaluator_1_result;
  wire [4:0] bus_decoder_1_rd, bus_decoder_1_rs1, bus_decoder_1_rs2;
  wire [6:0] bus_decoder_1_func7;
  wire [31:0] bus_decoder_1_imm, bus_decoder_1_pc, registers_v2_1_rs1out;
  wire [31:24] registers_v2_1_pc;
  wire [31:26] multiplexer_1_out;

  Multiplexer #(.width(32)) multiplexer_1 (
    .in1(ram_data), .out({multiplexer_1_out, address}), .sel(load));  // open: in0
  bus_decoder bus_decoder_1 (
    .instruction(instructions), .func3(func3), .func7(bus_decoder_1_func7), .rs1(bus_decoder_1_rs1),
    .rs2(bus_decoder_1_rs2), .rd(bus_decoder_1_rd), .imm(bus_decoder_1_imm), .pc(bus_decoder_1_pc),
    .is_imm(bus_decoder_1_is_imm), .jump(bus_decoder_1_jump), .store(bus_decoder_1_store), .load(clock),
    .clockload(bus_decoder_1_clockload), .alu(bus_decoder_1_alu), .cond(load), .load_ram(store));  // open: store_ram
  registers_v2 registers_v2_1 (
    .rs1out(registers_v2_1_rs1out), .rs2out(data), .pc({registers_v2_1_pc, pc}), .rd(bus_decoder_1_rd),
    .rs1(bus_decoder_1_rs1), .rs2(bus_decoder_1_rs2), .jump(condition_evaluator_1_result),
    .store(bus_decoder_1_jump), .load(bus_decoder_1_store), .clock(clock), .data({multiplexer_1_out, address}));
  ALU alu_1 (
    .func7(bus_decoder_1_func7), .rs1(registers_v2_1_rs1out), .rs2(data), .func3(func3),
    .imm_value(bus_decoder_1_imm), .immediate(bus_decoder_1_pc[0]), .is_active(bus_decoder_1_clockload),
    .rd({multiplexer_1_out, address}));
  condition_evaluator condition_evaluator_1 (
    .rs1(registers_v2_1_rs1out), .rs2(data), .func3(func3), .is_active(bus_decoder_1_alu),
    .result(condition_evaluator_1_result));
  // Pins of 1 and 32 bits meet at bus_decoder_1_pc
endmodule

module condition_evaluator (
  input  [31:0] rs1,
  input  [31:0] rs2,
  input  [2:0] func3,
  input  is_active,
  output result
);

  wire comparator_1_eq, comparator_1_gt, comparator_1_lt, comparator_2_eq, comparator_2_gt, comparator_2_lt,
       multiplexer_1_out, not_1_out, or_1_out, or_2_out;

  Comparator #(.width(32)) comparator_1 (
    .a(rs1), .b(rs2), .gt(comparator_1_gt), .eq(comparator_1_eq), .lt(comparator_1_lt));
  Comparator #(.mode("unsigned"), .width(32)) comparator_2 (
    .a(rs1), .b(rs2), .gt(comparator_2_gt), .eq(comparator_2_eq), .lt(comparator_2_lt));
  or or_1 (or_1_out, comparator_1_gt, comparator_1_eq);
  or or_2 (or_2_out, comparator_2_gt, comparator_2_eq);
  not not_1 (not_1_out, comparator_1_eq);
  Multiplexer #(.select(3)) multiplexer_1 (
    .in0(comparator_1_eq), .in1(not_1_out), .in4(comparator_1_lt), .in5(or_1_out), .in6(comparator_2_lt),
    .in7(or_2_out), .out(multiplexer_1_out), .sel(func3));  // open: in2, in3
  assign result = is_active ? multiplexer_1_out : 1'bz;  // Controlled_Buffer controlled_buffer_1
endmodule

module registers_v2 (
  input  [31:0] data,
  input  [4:0] rs1,
  input  [4:0] rs2,
  input  [4:0] rd,
  input  store,
  input  load,
  input  clock,
  input  jump,
  output [31:0] rs1out,
  output [31:0] rs2out,
  output [31:0] pc
);

  wire and_1_out, and_2_out, and_3_out, and_4_out, and_5_out, and_6_out, and_7_out, and_8_out, d_ff_1_q,
       nor_1_out, nor_2_out, nor_3_out, nor_4_out, not_1_out;
  wire [4:0] multiplexer_1_out, multiplexer_2_out;
  wire [31:0] ram_1_dout, ram_2_dout, register_1_q;

  and and_1 (and_1_out, rs1[0], rs1[1], rs1[2], rs1[3], rs1[4], and_6_out);
  nor nor_1 (nor_1_out, rs1[0], rs1[1], rs1[2], rs1[3], rs1[4]);
  nor nor_2 (nor_2_out, rs2[0], rs2[1], rs2[2], rs2[3], rs2[4]);
  and and_2 (and_2_out, rs2[0], rs2[1], rs2[2], rs2[3], rs2[4], and_6_out);
  and and_3 (and_3_out, and_6_out, nor_1_out);
  D_Flip_Flop d_ff_1 (.D(store), .clk(not_1_out), .Q(d_ff_1_q));  // open: Qn, preset, reset
  and and_4 (and_4_out, and_6_out, nor_2_out);
  Register #(.width(32)) register_1 (.D(data), .en(not_1_out), .clk(not_1_out), .Q(register_1_q));  // open: clr
  and and_5 (and_5_out, d_ff_1_q, not_1_out);
  and and_6 (and_6_out, load, clock);
  not not_1 (not_1_out, clock);
  RAM #(.addrWidth(5), .dataWidth(32), .trigger("high")) ram_1 (
    .addr(multiplexer_1_out), .we(and_5_out), .oe(and_6_out), .din(register_1_q), .dout(ram_1_dout));
  Multiplexer #(.width(5)) multiplexer_1 (.in0(rs1), .in1(rd), .out(multiplexer_1_out), .sel(not_1_out));
  RAM #(.addrWidth(5), .dataWidth(32), .trigger("high")) ram_2 (
    .addr(multiplexer_2_out), .we(and_5_out), .oe(and_6_out), .din(register_1_q), .dout(ram_2_dout));
  Multiplexer #(.width(5)) multiplexer_2 (.in0(rs2), .in1(rd), .out(multiplexer_2_out), .sel(not_1_out));
  nor nor_3 (nor_3_out, and_4_out, and_2_out);
  Counter #(.max('hffffffff), .width(32)) counter_1 (
    .load(jump), .D(register_1_q), .Q(pc), .clk(clock));  // open: count, carry, up, clr
  nor nor_4 (nor_4_out, and_1_out, and_3_out);
  assign rs1out = and_8_out ? ram_1_dout : 32'bz;  // Controlled_Buffer controlled_buffer_1
  assign rs2out = and_7_out ? ram_2_dout : 32'bz;  // Controlled_Buffer controlled_buffer_2
  and and_7 (and_7_out, nor_3_out, and_6_out);
  assign rs1out = and_3_out ? {32{1'b0}} : 32'bz;  // Controlled_Buffer controlled_buffer_3
  assign rs1out = and_1_out ? pc : 32'bz;  // Controlled_Buffer controlled_buffer_4
  and and_8 (and_8_out, nor_4_out, and_6_out);
  assign rs2out = and_2_out ? pc : 32'bz;  // Controlled_Buffer controlled_buffer_5
  assign rs2out = and_4_out ? {32{1'b0}} : 32'bz;  // Controlled_Buffer controlled_buffer_6
endmodule

module bus_decoder (
  input  [31:0] instruction,
  output [2:0] func3,
  output [6:0] func7,
  output [4:0] rs1,
  output [4:0] rs2,
  output [4:0] rd,
  output [31:0] imm,
  output [31:0] pc,
  output is_imm,
  output jump,
  output store,
  output load,
  output clockload,
  output alu,
  output cond,
  output load_ram,
  output store_ram
);

  wire demultiplexer_1_out4, demultiplexer_1_out8, demultiplexer_1_out12, demultiplexer_1_out27;

  Demultiplexer #(.select(5)) demultiplexer_1 (
    .out4(demultiplexer_1_out4), .out8(demultiplexer_1_out8), .out12(demultiplexer_1_out12),
    .out27(demultiplexer_1_out27), .in(1'b1), .sel(instruction[6:2]));  // open: out0, out1, out2, out3, out5, out6, out7, out9, out10, out11, out13, out14, out15, out16, out17, out18, out19, out20, out21, out22, out23, out24, out25, out26, out28, out29, out30, out31
  s_type s_type_1 (
    .instruction(instruction[31:7]), .active(demultiplexer_1_out8), .funct3(func3), .rs1(rs1), .rs2(rs2),
    .imm_11_0(imm), .load(jump), .alu(alu), .store_ram(store_ram), .imm_on(is_imm));
  i_type i_type_1 (
    .instruction(instruction[31:7]), .is_active(demultiplexer_1_out4), .rd(rd), .funct3(func3), .rs1(rs1),
    .imm_11_0(imm), .load(jump), .store(store), .alu(alu), .imm_on(is_imm));
  r_type r_type_1 (
    .instruction(instruction[31:7]), .is_active(demultiplexer_1_out12), .rd(rd), .funct3(func3), .rs1(rs1),
    .rs2(rs2), .funct7(func7), .store(store), .load(jump), .alu(alu));
  // uj_type uj_type_1: pin names not known; wires that end beside it: instruction[31:7], demultiplexer_1_out27, rs1, rd, imm, pc, jump, jump, jump, jump
  Clock clock_1 (.out(clockload));

  assign load = jump;
endmodule

module r_type (
  input  [24:0] instruction,
  input  is_active,
  output [4:0] rd,
  output [2:0] funct3,
  output [4:0] rs1,
  output [4:0] rs2,
  output [6:0] funct7,
  output store,
  output load,
  output alu
);

  assign {funct7, rs2, rs1, funct3, rd} = is_active ? instruction : 25'bz;  // Controlled_Buffer controlled_buffer_1
  assign alu = is_active ? is_active : 1'bz;  // Controlled_Buffer controlled_buffer_2

  assign load = alu;
  assign store = alu;
endmodule

module i_type (
  input  [24:0] instruction,
  input  is_active,
  output [4:0] rd,
  output [2:0] funct3,
  output [4:0] rs1,
  output [31:0] imm_11_0,
  output load,
  output store,
  output alu,
  output imm_on
);

  assign {imm_11_0[11:0], rs1, funct3, rd} = is_active ? instruction : 25'bz;  // Controlled_Buffer controlled_buffer_1
  assign alu = is_active ? is_active : 1'bz;  // Controlled_Buffer controlled_buffer_2

  assign imm_on = alu;
  assign load = alu;
  assign store = alu;
endmodule

module s_type (
  input  [24:0] instruction,
  input  active,
  output [2:0] funct3,
  output [4:0] rs1,
  output [4:0] rs2,
  output [31:0] imm_11_0,
  output load,
  output alu,
  output store_ram,
  output imm_on
);

  assign {imm_11_0[11:5], rs2, rs1, funct3, imm_11_0[4:0]} = active ? instruction : 25'bz;  // Controlled_Buffer controlled_buffer_1
  assign alu = active ? active : 1'bz;  // Controlled_Buffer controlled_buffer_2

  assign imm_on = alu;
  assign load = alu;
  assign store_ram = alu;
endmodule

module uj_type (
  input  [24:0] instruction,
  input  active,
  output [4:0] rs1,
  output [4:0] rd,
  output [31:0] imm,
  output [31:0] pc,
  output store,
  output load,
  output jump,
  output alu
);

  assign {pc[19], pc[9:0], pc[10], pc[18:11], rd} = active ? instruction : 25'bz;  // Controlled_Buffer controlled_buffer_1
  assign rs1 = active ? {5{1'b1}} : 5'bz;  // Controlled_Buffer controlled_buffer_2
  assign alu = active ? active : 1'bz;  // Controlled_Buffer controlled_buffer_3
  assign imm = active ? 32'h1 : 32'bz;  // Controlled_Buffer controlled_buffer_4

  assign jump = alu;
  assign load = alu;
  assign store = alu;
endmodule
