// Logisim project ComputerV1.circ as structural Verilog
module main (
);

  wire clock_1_out;
  wire [7:0] program_counter_q;
  wire [31:0] program_data;

  Clock clock_1 (.out(clock_1_out));
  Counter program_counter (.up(1'b1), .clk(clock_1_out), .Q(program_counter_q));  // open: clr, load, count, D, carry
  ROM #(.dataWidth(32)) \program  (.addr(program_counter_q), .data(program_data));
  cpu cpu_1 (.instruction(program_data));

  // Notes on the sheet:
  //   contents of program (hex, n*v repeats v):
  //   ff00193 f1f113 ff14093 f0e193 208233 40320233 11f233 226233 324233 112233 12213 113233 13213 400293
  //   511233 525233 421213 425213 425233 4012d293 4052d2b3 1237 217 26f 420267 7213 21463 6f 100463 6f
  //   115463 6f 20f463 6f 24463 6f 26463 6f 300223 3002a3 300323 3003a3 400203 2223 402203
endmodule

module cpu (
  input  [31:0] instruction
);

  wire [24:0] demultiplexer_1_out1;

  // Probe on instruction[6:0]
  // Probe on instruction[31:7]
  // Probe on instruction[6:4]
  Demultiplexer #(.select(3), .width(25)) demultiplexer_1 (
    .out1(demultiplexer_1_out1), .in(instruction[31:7]), .sel(instruction[6:4]));  // open: out0, out2, out3, out4, out5, out6, out7
  fmt_i fmt_i_1 (.instruction(demultiplexer_1_out1));  // open: rd, funct3, rs1, imm_11_0
endmodule

module fmt_i (
  input  [24:0] instruction,
  output [4:0] rd,
  output [2:0] funct3,
  output [4:0] rs1,
  output [11:0] imm_11_0
);


  assign funct3 = instruction[7:5];
  assign imm_11_0 = instruction[24:13];
  assign rd = instruction[4:0];
  assign rs1 = instruction[12:8];
endmodule
